# Fritzing sketch abastecimento inteligente (saved by Fritzing 0.9.3b)
circuit board: 13.0303cm x 5.85174cm
breadboards: 2

parts:
  IA = Arduino Uno (Rev3)
  LED1 = LED - 5mm [color="Red (633nm)" package="5 mm [THT]"]
  LED2 = LED - 5mm [color="Blue (525nm)" package="5 mm [THT]"]
  LED3 = LED - 5mm [color="Yellow (595nm)" package="5 mm [THT]"]
  LED4 = LED - 5mm [color="Green (565nm)" package="5 mm [THT]"]
  R1 = Resistor [tolerance=±5% resistance=220 package=THT]
  R2 = Resistor [tolerance=±5% resistance=220 package=THT]
  R3 = Resistor [tolerance=±5% resistance=220 package=THT]
  R4 = Resistor [tolerance=±5% resistance=220 package=THT]
  Relé = Keyes Relay [package=THT]
  S1 = Pushbutton [package="[THT]"]
  R5 = Resistor [tolerance=±5% resistance=150 package=THT]
  S3 = Pushbutton [package="[THT]"]
  R8 = Resistor [tolerance=±5% resistance=150 package=THT]
  R10 = Resistor [tolerance=±5% resistance=10k package=THT]
  S5 = Pushbutton [package="[THT]"]
  R12 = Resistor [tolerance=±5% resistance=150 package=THT]
  R14 = Resistor [tolerance=±5% resistance=10k package=THT]
  S7 = Pushbutton [package="[THT]"]
  R16 = Resistor [tolerance=±5% resistance=150 package=THT]
  R18 = Resistor [tolerance=±5% resistance=10k package=THT]
  R6 = Resistor [tolerance=±5% resistance=10k package=THT]

nets (from the pcb view):
  N1: IA.D8, R16.Pin_1
  N2: IA.D9_PWM, Relé.signal
  N3: IA.D10_PWM/SS, LED1.cathode
  N4: IA.D11_PWM/MOSI, LED2.cathode
  N5: IA.D12/MISO, LED3.cathode
  N6: IA.D13/SCK, LED4.cathode
  N7: IA.GND, R1.Pin_1, R2.Pin_1, R3.Pin_1, R4.Pin_1, Relé.ground, R10.Pin_1, R14.Pin_1, R18.Pin_1, R6.Pin_1
  N8: IA.D5_PWM, R5.Pin_1
  N9: IA.D6_PWM, R8.Pin_1
  N10: IA.D7, R12.Pin_1
  N11: IA.5V, Relé.NC, S1.Pin_3, S1.Pin_4, R5.Pin_0, S3.Pin_3, S3.Pin_4, R8.Pin_0, R10.Pin_0, S5.Pin_3, S5.Pin_4, R12.Pin_0, R14.Pin_0, S7.Pin_3, S7.Pin_4, R16.Pin_0, R18.Pin_0, R6.Pin_0
  N12: LED1.anode, R1.Pin_0
  N13: LED2.anode, R2.Pin_0
  N14: LED3.anode, R3.Pin_0
  N15: LED4.anode, R4.Pin_0
  N16: S1.Pin_1, S1.Pin_2
  N17: S3.Pin_1, S3.Pin_2
  N18: S5.Pin_1, S5.Pin_2
  N19: S7.Pin_1, S7.Pin_2

custom parts:
  Keyes Relay: The Keyes 5V relay module is suitable for SCM development, home appliance control. It uses a 5V~12V TIL control signal which can control DC / AC signal.
